// Digital circuit CPU.dig as structural Verilog
module CPU (
  input  clk,
  input  CLR_PC
);

  wire comparator_1_eq, comparator_2_eq, comparator_3_eq, comparator_4_eq, comparator_5_eq, comparator_6_eq,
       comparator_7_eq, comparator_8_eq, comparator_9_eq, comparator_10_eq, comparator_11_eq,
       comparator_12_eq, comparator_13_eq;
  wire [7:0] rom_1_d, rom_2_d;
  wire [15:0] programme_counter_1_ln, rom_3_d;

  Comparator #(.Bits(8)) comparator_1 (.a(rom_1_d), .b(8'h1), .eq(comparator_1_eq));  // open: gt, lt
  Comparator #(.Bits(8)) comparator_2 (.a(rom_1_d), .b(8'h2), .eq(comparator_2_eq));  // open: gt, lt
  Comparator #(.Bits(8)) comparator_3 (.a(rom_1_d), .b(8'h3), .eq(comparator_3_eq));  // open: gt, lt
  Comparator #(.Bits(8)) comparator_4 (.a(rom_1_d), .b(8'h4), .eq(comparator_4_eq));  // open: gt, lt
  Comparator #(.Bits(8)) comparator_5 (.a(rom_1_d), .b(8'h5), .eq(comparator_5_eq));  // open: gt, lt
  Comparator #(.Bits(8)) comparator_6 (.a(rom_1_d), .b(8'h6), .eq(comparator_6_eq));  // open: gt, lt
  Comparator #(.Bits(8)) comparator_7 (.a(rom_1_d), .b(8'h7), .eq(comparator_7_eq));  // open: gt, lt
  Comparator #(.Bits(8)) comparator_8 (.a(rom_1_d), .b(8'h8), .eq(comparator_8_eq));  // open: gt, lt
  Comparator #(.Bits(8)) comparator_9 (.a(rom_1_d), .b(8'h9), .eq(comparator_9_eq));  // open: gt, lt
  Comparator #(.Bits(8)) comparator_10 (.a(rom_1_d), .b(8'ha), .eq(comparator_10_eq));  // open: gt, lt
  Comparator #(.Bits(8)) comparator_11 (.a(rom_1_d), .b(8'hb), .eq(comparator_11_eq));  // open: gt, lt
  Comparator #(.Bits(8)) comparator_12 (.a(rom_1_d), .b(8'hc), .eq(comparator_12_eq));  // open: gt, lt
  Comparator #(.Bits(8)) comparator_13 (.a(rom_1_d), .b(8'hd), .eq(comparator_13_eq));  // open: gt, lt
  Programme_Counter programme_counter_1 (
    .DAT(rom_2_d), .CLK(clk), .STJ_1(comparator_1_eq), .STJ_2(comparator_2_eq), .JMP(comparator_3_eq),
    .CJP(comparator_4_eq), .CLR(CLR_PC), .LN(programme_counter_1_ln));
  ROM #(.AddrBits(16), .Bits(8)) rom_1 (.A(programme_counter_1_ln), .sel(1'b1), .D(rom_1_d));
  ROM #(.AddrBits(16), .Bits(8)) rom_2 (.A(programme_counter_1_ln), .sel(1'b1), .D(rom_2_d));
  ROM #(.AddrBits(16), .Bits(16)) rom_3 (.A(programme_counter_1_ln), .sel(1'b1), .D(rom_3_d));
  ALU alu_1 (.CMD(rom_1_d), .DAT(rom_2_d), .CLK(clk), .Q(rom_2_d));
  RAM ram_1 (
    .DAT(rom_2_d), .ADR(rom_3_d), .STR_reg1(comparator_5_eq), .STR_reg2(comparator_6_eq),
    .STR(comparator_7_eq), .LD(comparator_8_eq), .STR_todata(comparator_9_eq),
    .LD_fromdata(comparator_10_eq), .LD_reg1(comparator_11_eq), .LD_reg2(comparator_12_eq),
    .LD_toaddrbus(comparator_13_eq), .CLK(clk), .Q_DAT(rom_2_d), .Q_ADR(rom_3_d));

  // Notes on the sheet:
  //   clk: Hz: 20
  //   LN
  //   CMD
  //   LN: output from the programmme counter,
  //   the current line of code being executed
  //   DAT
  //   ADR
  //   CLK
  //   - Flash memory
endmodule
